# Fritzing sketch ProximitySketch (saved by Fritzing 0.9.3b)
breadboards: 1

parts:
  Componente1 = Arduino Uno (Rev3)
  hc-sr1 = hc-sr04
  LED1 = LED - 5mm [color="Yellow (585nm)" package="5 mm [THT]"]
  LED2 = LED - 5mm [color="Green (565nm)" package="5 mm [THT]"]
  LED3 = LED - 5mm [color="Red (633nm)" package="5 mm [THT]"]
  R1 = Resistor [tolerance=±5% resistance=1k package=THT]
  R2 = Resistor [tolerance=±5% resistance=1k package=THT]
  R3 = Resistor [tolerance=±5% resistance=1k package=THT]

nets:
  N1: Componente1.D9_PWM, LED1.anode
  N2: Componente1.D10_PWM/SS, LED2.anode
  N3: Componente1.D11_PWM/MOSI, LED3.anode
  GND: Componente1.GND, hc-sr1.GND, R1.Pin_0, R2.Pin_0, R3.Pin_0
  N4: Componente1.D3_PWM, hc-sr1.Trig
  N5: Componente1.D7, hc-sr1.Echo
  5V: Componente1.5V, hc-sr1.VCC
  N6: LED1.cathode, R1.Pin_1
  N7: LED2.cathode, R3.Pin_1
  N8: LED3.cathode, R2.Pin_1
