# Fritzing sketch PlayerLEDSketch (saved by Fritzing 0.9.3b)
breadboards: 1

parts:
  R = Resistor [tolerance=±5% resistance=220 package=THT]
  LED = LED - 5mm [color="Red (633nm)" package="5 mm [THT]"]
  LilyPad_Board = LilyPad Arduino USB

nets:
  N1: R.Pin_0, LilyPad_Board.GND
  N2: R.Pin_1, LED.cathode
  N3: LED.anode, LilyPad_Board.A5

notes:
  T5
  GND
  Suppose A5 = T5
